// Logisim project circuito.circ as structural Verilog: 20 circuits, main circuit main
module main (
  input  B3,
  input  B2,
  input  B1,
  input  B0,
  input  A3,
  input  A2,
  input  A1,
  input  A0
);

  wire and_1_out, and_2_out, CHUTAR_out, clock_1_out, core_1_a_jogando, core_1_acertou, core_1_b_jogando,
       core_1_chutando_x, core_1_chutando_y, core_1_igual, core_1_maior, core_1_menor, DMA_out, DMB_out,
       DSA_out, DSB_out, MODE_out, negativo_1_neg, negativo_2_neg, negativo_3_neg, negativo_4_neg,
       PROXIMO_out, relogios_1_zerou_a, relogios_1_zerou_b, RESET_out, START_out, UMA_out, UMB_out, USA_out,
       USB_out;
  wire [3:0] \core_1_saída_x , \core_1_saída_y , negativo_1_out_2, negativo_2_out_2, negativo_3_out_2,
       negativo_4_out_2, \placar_1_saída , \placar_2_saída , relogios_1_dma_3, relogios_1_dmb,
       relogios_1_dsa_3, relogios_1_dsb, relogios_1_uma_3, relogios_1_umb, relogios_1_usa_3, relogios_1_usb;

  Button START (.out(START_out));
  Clock clock_1 (.out(clock_1_out));
  Button MODE (.out(MODE_out));
  Button RESET (.out(RESET_out));
  Button PROXIMO (.out(PROXIMO_out));
  Button CHUTAR (.out(CHUTAR_out));
  LED JOGANDO (.in(core_1_a_jogando));
  Hex_Digit_Display hex_digit_display_1 (.value(\placar_1_saída ));  // open: dp
  PLACAR placar_1 (.CLK(and_1_out), .RESET(RESET_out), .\SAÍDA (\placar_1_saída ));
  Hex_Digit_Display hex_digit_display_2 (.value(relogios_1_uma_3));  // open: dp
  Hex_Digit_Display hex_digit_display_3 (.value(relogios_1_dma_3));  // open: dp
  Button UMA (.out(UMA_out));
  Button DMA (.out(DMA_out));
  LED SA (.in(negativo_1_neg));
  NEGATIVO negativo_1 (.A({A3, A2, A1, A0}), .out_2(negativo_1_out_2), .NEG(negativo_1_neg));
  and and_1 (and_1_out, ~core_1_a_jogando, core_1_acertou);  // AND_Gate
  LED led_1 (.in(1'b1));
  LED led_2 (.in(1'b1));
  Hex_Digit_Display hex_digit_display_4 (.value(relogios_1_dsa_3));  // open: dp
  Button DSA (.out(DSA_out));
  Button USA (.out(USA_out));
  Hex_Digit_Display hex_digit_display_5 (.value(negativo_1_out_2));  // open: dp
  Hex_Digit_Display hex_digit_display_6 (.value(relogios_1_usa_3));  // open: dp
  LED CHUTANDO_X (.in(core_1_chutando_x));
  LED SX (.in(negativo_2_neg));
  Hex_Digit_Display hex_digit_display_7 (.value(negativo_2_out_2));  // open: dp
  NEGATIVO negativo_2 (.A(\core_1_saída_x ), .out_2(negativo_2_out_2), .NEG(negativo_2_neg));
  LED MAIOR (.in(core_1_maior));
  LED IGUAL (.in(core_1_igual));
  LED ACERTOU (.in(core_1_acertou));
  RELOGIOS relogios_1 (
    .START(START_out), .CLK(clock_1_out), .MODE(MODE_out), .RESET(RESET_out),
    .SWITCH_PLAYER(core_1_chutando_x), .DMA_3(relogios_1_dma_3), .UMA_3(relogios_1_uma_3),
    .DSA_3(relogios_1_dsa_3), .USA_3(relogios_1_usa_3), .DMB(relogios_1_dmb), .UMB(relogios_1_umb),
    .DSB(relogios_1_dsb), .USB(relogios_1_usb), .ZEROU_A(relogios_1_zerou_a), .ZEROU_B(relogios_1_zerou_b),
    .DMA(DMA_out), .UMA(UMA_out), .DSA(DSA_out), .USA(USA_out), .DMA_2(DMB_out), .UMA_2(UMB_out),
    .DSA_2(DSB_out), .USA_2(USB_out));
  CORE core_1 (
    .PROXIMO(PROXIMO_out), .CLOCK_GERADOR(core_1_acertou), .\SAÍDA_X (\core_1_saída_x ),
    .MAIOR(core_1_maior), .IGUAL(core_1_igual), .MENOR(core_1_menor), .\SAÍDA_Y (\core_1_saída_y ),
    .ACERTOU(core_1_acertou), .A_JOGANDO(core_1_a_jogando), .B_JOGANDO(core_1_b_jogando),
    .CHUTANDO_X(core_1_chutando_x), .CHUTANDO_Y(core_1_chutando_y), .A({A3, A2, A1, A0}),
    .B({B3, B2, B1, B0}), .ZEROU_A(relogios_1_zerou_a), .ZEROU_B(relogios_1_zerou_b), .CHUTAR(CHUTAR_out));  // open: SOMA, X_REAL, Y_REAL
  LED MENOR (.in(core_1_menor));
  LED CHUTANDO_Y (.in(core_1_chutando_y));
  LED SY (.in(negativo_3_neg));
  NEGATIVO negativo_3 (.A(\core_1_saída_y ), .out_2(negativo_3_out_2), .NEG(negativo_3_neg));
  Hex_Digit_Display hex_digit_display_8 (.value(relogios_1_dmb));  // open: dp
  Hex_Digit_Display hex_digit_display_9 (.value(negativo_3_out_2));  // open: dp
  LED led_3 (.in(1'b1));
  LED led_4 (.in(1'b1));
  Hex_Digit_Display hex_digit_display_10 (.value(relogios_1_umb));  // open: dp
  Button DSB (.out(DSB_out));
  Button DMB (.out(DMB_out));
  Button UMB (.out(UMB_out));
  LED JOGANDO_2 (.in(core_1_b_jogando));
  and and_2 (and_2_out, ~core_1_b_jogando, core_1_acertou);  // AND_Gate
  Hex_Digit_Display hex_digit_display_11 (.value(relogios_1_usb));  // open: dp
  Hex_Digit_Display hex_digit_display_12 (.value(relogios_1_dsb));  // open: dp
  Button USB (.out(USB_out));
  PLACAR placar_2 (.CLK(and_2_out), .RESET(RESET_out), .\SAÍDA (\placar_2_saída ));
  LED SA_2 (.in(negativo_4_neg));
  Hex_Digit_Display hex_digit_display_13 (.value(negativo_4_out_2));  // open: dp
  NEGATIVO negativo_4 (.A({B3, B2, B1, B0}), .out_2(negativo_4_out_2), .NEG(negativo_4_neg));
  Hex_Digit_Display hex_digit_display_14 (.value(\placar_2_saída ));  // open: dp

  // Notes on the sheet:
  //   PLACAR A
  //   JOGADOR A
  //   CHUTE X
  //   CHUTE Y
  //   JOGADOR B
  //   PLACAR B
endmodule

module MUX (
  input  [3:0] A,
  input  [3:0] B,
  input  SELETOR,
  output [3:0] \SAÍDA 
);

  wire [3:0] and_1_out, and_2_out, not_1_out;

  assign and_1_out = A & not_1_out;  // AND_Gate and_1, 4 bits wide
  assign not_1_out = ~{4{SELETOR}};  // NOT_Gate not_1, 4 bits wide
  assign and_2_out = B & {4{SELETOR}};  // AND_Gate and_2, 4 bits wide
  assign \SAÍDA  = and_1_out | and_2_out;  // OR_Gate or_1, 4 bits wide
endmodule

module XOR (
  input  A,
  input  B,
  input  C,
  output \SAÍDA 
);

  wire and_1_out, and_2_out, and_3_out, and_4_out, or_1_out;

  and and_1 (and_1_out, ~A, B);  // AND_Gate
  and and_2 (and_2_out, A, ~B);  // AND_Gate
  or or_1 (or_1_out, and_1_out, and_2_out);
  and and_3 (and_3_out, ~or_1_out, C);  // AND_Gate
  and and_4 (and_4_out, or_1_out, ~C);  // AND_Gate
  or or_2 (\SAÍDA , and_3_out, and_4_out);
endmodule

// SUM
module SOMADOR (
  input  [3:0] A,
  input  [3:0] B,
  output [3:0] SUM,
  output CARRY
);

  wire and_1_out, and_2_out, and_3_out, and_4_out, and_5_out, and_6_out, and_7_out, and_8_out, and_9_out,
       and_10_out, and_11_out, and_12_out, or_1_out, or_2_out, or_3_out;

  and and_1 (and_1_out, A[0], B[0]);
  and and_2 (and_2_out, A[0], 1'b0);
  and and_3 (and_3_out, B[0], 1'b0);
  XOR xor_1 (.A(1'b0), .B(A[0]), .C(B[0]), .\SAÍDA (SUM[0]));
  or or_1 (or_1_out, and_1_out, and_2_out, and_3_out);
  XOR xor_2 (.A(or_1_out), .B(A[1]), .C(B[1]), .\SAÍDA (SUM[1]));
  and and_4 (and_4_out, A[1], B[1]);
  and and_5 (and_5_out, A[1], or_1_out);
  and and_6 (and_6_out, or_1_out, B[1]);
  or or_2 (or_2_out, and_4_out, and_5_out, and_6_out);
  XOR xor_3 (.A(or_2_out), .B(A[2]), .C(B[2]), .\SAÍDA (SUM[2]));
  and and_7 (and_7_out, A[2], B[2]);
  and and_8 (and_8_out, A[2], or_2_out);
  and and_9 (and_9_out, or_2_out, B[2]);
  or or_3 (or_3_out, and_7_out, and_8_out, and_9_out);
  XOR xor_4 (.A(or_3_out), .B(A[3]), .C(B[3]), .\SAÍDA (SUM[3]));
  and and_10 (and_10_out, A[3], B[3]);
  and and_11 (and_11_out, A[3], or_3_out);
  and and_12 (and_12_out, or_3_out, B[3]);
  or or_4 (CARRY, and_10_out, and_11_out, and_12_out);
endmodule

// FFD
module FLIP_FLOP_D (
  input  D,
  input  CLK,
  input  ENABLE,
  input  PRESET,
  input  CLEAR,
  output Q
);

  wire and_1_out, and_2_out, and_3_out, nor_2_out, not_1_out, not_2_out, not_3_out, not_4_out, or_1_out,
       or_2_out;

  not not_1 (not_1_out, CLK);
  not not_2 (not_2_out, not_3_out);
  not not_3 (not_3_out, not_1_out);
  and and_1 (and_1_out, not_2_out, CLK, ENABLE);
  not not_4 (not_4_out, D);
  and and_2 (and_2_out, not_4_out, and_1_out);
  and and_3 (and_3_out, and_1_out, D);
  or or_1 (or_1_out, CLEAR, and_2_out);
  or or_2 (or_2_out, and_3_out, PRESET);
  nor nor_1 (Q, or_1_out, nor_2_out);
  nor nor_2 (nor_2_out, Q, or_2_out);
endmodule

// REGIS
module REGISTRADOR (
  input  [3:0] D,
  input  CLK,
  input  ENABLE,
  input  CLEAR,
  input  ACTIVATE_PRESET,
  input  [3:0] PRESET,
  output [3:0] \SAÍDA 
);

  wire and_1_out, and_2_out, and_3_out, and_4_out, or_1_out, or_2_out, or_3_out, or_4_out;
  wire [3:0] \mux_1_saída ;

  FLIP_FLOP_D flip_flop_d_1 (
    .D(D[0]), .CLK(CLK), .ENABLE(ENABLE), .PRESET(\mux_1_saída [0]), .CLEAR(or_1_out), .Q(\SAÍDA [0]));
  or or_1 (or_1_out, and_1_out, CLEAR);
  and and_1 (and_1_out, ~\mux_1_saída [0], ACTIVATE_PRESET);  // AND_Gate
  FLIP_FLOP_D flip_flop_d_2 (
    .D(D[1]), .CLK(CLK), .ENABLE(ENABLE), .PRESET(\mux_1_saída [1]), .CLEAR(or_2_out), .Q(\SAÍDA [1]));
  or or_2 (or_2_out, and_2_out, CLEAR);
  and and_2 (and_2_out, ~\mux_1_saída [1], ACTIVATE_PRESET);  // AND_Gate
  MUX mux_1 (.A(4'b0000), .B(PRESET), .SELETOR(ACTIVATE_PRESET), .\SAÍDA (\mux_1_saída ));
  FLIP_FLOP_D flip_flop_d_3 (
    .D(D[2]), .CLK(CLK), .ENABLE(ENABLE), .PRESET(\mux_1_saída [2]), .CLEAR(or_3_out), .Q(\SAÍDA [2]));
  or or_3 (or_3_out, and_3_out, CLEAR);
  and and_3 (and_3_out, ~\mux_1_saída [2], ACTIVATE_PRESET);  // AND_Gate
  FLIP_FLOP_D flip_flop_d_4 (
    .D(D[3]), .CLK(CLK), .ENABLE(ENABLE), .PRESET(\mux_1_saída [3]), .CLEAR(or_4_out), .Q(\SAÍDA [3]));
  or or_4 (or_4_out, and_4_out, CLEAR);
  and and_4 (and_4_out, ~\mux_1_saída [3], ACTIVATE_PRESET);  // AND_Gate
endmodule

// =
module IGUAL (
  input  [3:0] A,
  input  [3:0] B,
  output \SAÍDA 
);

  wire xnor_1_out, xnor_2_out, xnor_3_out, xnor_4_out;

  xnor xnor_1 (xnor_1_out, B[0], A[0]);
  xnor xnor_2 (xnor_2_out, B[1], A[1]);
  xnor xnor_3 (xnor_3_out, B[2], A[2]);
  xnor xnor_4 (xnor_4_out, B[3], A[3]);
  and and_1 (\SAÍDA , xnor_1_out, xnor_2_out, xnor_3_out, xnor_4_out);
endmodule

// PRE
module PRESET (
  input  CLK,
  input  [3:0] MAXIMO,
  input  CLEAR,
  output [3:0] \SAÍDA 
);

  wire \igual_1_saída ;
  wire [3:0] \mux_1_saída , somador_1_sum;

  REGISTRADOR registrador_1 (
    .D(\mux_1_saída ), .CLK(CLK), .PRESET(4'b0000), .ENABLE(1'b1), .ACTIVATE_PRESET(1'b0), .CLEAR(CLEAR),
    .\SAÍDA (\SAÍDA ));
  SOMADOR somador_1 (.A(\SAÍDA ), .B(4'b0001), .SUM(somador_1_sum));  // open: CARRY
  IGUAL igual_1 (.\SAÍDA (\igual_1_saída ), .A(somador_1_sum), .B(MAXIMO));
  MUX mux_1 (.A(somador_1_sum), .B(4'b0000), .SELETOR(\igual_1_saída ), .\SAÍDA (\mux_1_saída ));
endmodule

// UNI
module UNIDADES (
  input  [3:0] E,
  output [3:0] E_plus,
  output S
);

  wire and_1_out, and_2_out, and_3_out, and_4_out, and_5_out, and_6_out, and_7_out, and_8_out, and_9_out,
       and_10_out, and_11_out, and_12_out, and_13_out, and_14_out, and_15_out, not_1_out, not_2_out,
       not_3_out, not_4_out, not_5_out, not_6_out, not_7_out, not_8_out, not_9_out, not_10_out, not_11_out,
       not_12_out, not_13_out, not_14_out, not_15_out, not_16_out, not_17_out;

  not not_1 (not_1_out, E[3]);
  not not_2 (not_2_out, E[2]);
  not not_3 (not_3_out, E[1]);
  not not_4 (not_4_out, E[0]);
  not not_5 (not_5_out, E[3]);
  not not_6 (not_6_out, E[3]);
  not not_7 (not_7_out, E[2]);
  not not_8 (not_8_out, E[1]);
  not not_9 (not_9_out, E[0]);
  not not_10 (not_10_out, E[3]);
  not not_11 (not_11_out, E[3]);
  not not_12 (not_12_out, E[1]);
  not not_13 (not_13_out, E[0]);
  not not_14 (not_14_out, E[2]);
  not not_15 (not_15_out, E[1]);
  not not_16 (not_16_out, E[0]);
  not not_17 (not_17_out, E[0]);
  and and_1 (and_1_out, E[3], E[1]);
  and and_2 (and_2_out, E[3], E[2]);
  and and_3 (and_3_out, not_1_out, not_2_out, not_3_out, not_4_out);
  and and_4 (and_4_out, E[3], E[0]);
  and and_5 (and_5_out, E[3], E[1]);
  and and_6 (and_6_out, E[3], E[2]);
  and and_7 (and_7_out, not_5_out, E[2], E[0]);
  and and_8 (and_8_out, not_6_out, E[2], E[1]);
  and and_9 (and_9_out, E[3], not_7_out, not_8_out, not_9_out);
  and and_10 (and_10_out, not_10_out, E[1], E[0]);
  and and_11 (and_11_out, not_11_out, E[2], not_12_out, not_13_out);
  and and_12 (and_12_out, E[3], not_14_out, not_15_out, not_16_out);
  or or_1 (E_plus[0], not_17_out, and_1_out, and_2_out);
  and and_13 (and_13_out, E[3], E[0]);
  and and_14 (and_14_out, E[3], E[1]);
  and and_15 (and_15_out, E[3], E[2]);
  or or_2 (E_plus[3], and_3_out, and_4_out, and_5_out, and_6_out);
  or or_3 (E_plus[2], and_7_out, and_8_out, and_9_out);
  or or_4 (E_plus[1], and_10_out, and_11_out, and_12_out);
  or or_5 (S, and_13_out, and_14_out, and_15_out);
endmodule

// DEZ
module DEZENAS (
  input  [3:0] E,
  output [3:0] E_plus,
  output S
);

  wire and_1_out, and_2_out, and_3_out, and_4_out, and_5_out, and_6_out, and_7_out, and_8_out, not_1_out,
       not_2_out, not_3_out, not_4_out, not_5_out, not_6_out, not_7_out, not_8_out, not_9_out;

  not not_1 (not_1_out, E[2]);
  and and_1 (and_1_out, not_1_out, not_2_out, not_3_out);
  not not_2 (not_2_out, E[1]);
  not not_3 (not_3_out, E[0]);
  and and_2 (and_2_out, E[2], E[0]);
  and and_3 (and_3_out, E[2], E[1]);
  not not_4 (not_4_out, E[3]);
  not not_5 (not_5_out, E[2]);
  not not_6 (not_6_out, E[3]);
  not not_7 (not_7_out, E[1]);
  not not_8 (not_8_out, E[0]);
  not not_9 (not_9_out, E[0]);
  and and_4 (and_4_out, E[2], E[1]);
  and and_5 (and_5_out, E[2], E[1]);
  and and_6 (and_6_out, E[2], E[0]);
  or or_1 (E_plus[2], and_1_out, and_2_out, and_3_out, E[3]);
  and and_7 (and_7_out, not_4_out, not_5_out, E[1], E[0]);
  or or_2 (E_plus[1], and_7_out, and_8_out);
  and and_8 (and_8_out, not_6_out, E[2], not_7_out, not_8_out);
  or or_3 (E_plus[0], not_9_out, and_4_out, E[3]);
  or or_4 (S, E[3], and_5_out, and_6_out);

  assign E_plus[3] = 1'b0;
endmodule

// CONTADOR
module CONTADOR_REGRESSIVO (
  input  CLK,
  input  [3:0] PRESET_US,
  input  [3:0] PRESET_DS,
  input  [3:0] PRESET_UM,
  input  [3:0] PRESET_DM,
  input  ENABLE,
  input  ACTIVATE_PRESET,
  input  CLEAR,
  output [3:0] US,
  output [3:0] DS,
  output [3:0] UM,
  output [3:0] DM,
  output ZEROU
);

  wire dezenas_1_s, \igual_1_saída , \igual_2_saída , \igual_3_saída , \igual_4_saída , unidades_1_s,
       unidades_2_s;
  wire [3:0] dezenas_1_e_plus, dezenas_2_e_plus, unidades_1_e_plus, unidades_2_e_plus;

  Hex_Digit_Display hex_digit_display_1 (.value(US));  // open: dp
  REGISTRADOR registrador_1 (
    .D(unidades_1_e_plus), .CLK(CLK), .PRESET(PRESET_US), .ENABLE(ENABLE), .ACTIVATE_PRESET(ACTIVATE_PRESET),
    .CLEAR(CLEAR), .\SAÍDA (US));
  UNIDADES unidades_1 (.E(US), .E_plus(unidades_1_e_plus), .S(unidades_1_s));
  REGISTRADOR registrador_2 (
    .D(dezenas_1_e_plus), .CLK(unidades_1_s), .PRESET(PRESET_DS), .ENABLE(ENABLE),
    .ACTIVATE_PRESET(ACTIVATE_PRESET), .CLEAR(CLEAR), .\SAÍDA (DS));
  Hex_Digit_Display hex_digit_display_2 (.value(DS));  // open: dp
  DEZENAS dezenas_1 (.E(DS), .E_plus(dezenas_1_e_plus), .S(dezenas_1_s));
  Hex_Digit_Display hex_digit_display_3 (.value(UM));  // open: dp
  REGISTRADOR registrador_3 (
    .D(unidades_2_e_plus), .CLK(dezenas_1_s), .PRESET(PRESET_UM), .ENABLE(ENABLE),
    .ACTIVATE_PRESET(ACTIVATE_PRESET), .CLEAR(CLEAR), .\SAÍDA (UM));
  UNIDADES unidades_2 (.E(UM), .E_plus(unidades_2_e_plus), .S(unidades_2_s));
  Hex_Digit_Display hex_digit_display_4 (.value(DM));  // open: dp
  REGISTRADOR registrador_4 (
    .D(dezenas_2_e_plus), .CLK(unidades_2_s), .PRESET(PRESET_DM), .ENABLE(ENABLE),
    .ACTIVATE_PRESET(ACTIVATE_PRESET), .CLEAR(CLEAR), .\SAÍDA (DM));
  DEZENAS dezenas_2 (.E(DM), .E_plus(dezenas_2_e_plus));  // open: S
  IGUAL igual_1 (.\SAÍDA (\igual_1_saída ), .A(DM), .B(4'b0000));
  IGUAL igual_2 (.\SAÍDA (\igual_2_saída ), .A(UM), .B(4'b0000));
  IGUAL igual_3 (.\SAÍDA (\igual_3_saída ), .A(DS), .B(4'b0000));
  IGUAL igual_4 (.\SAÍDA (\igual_4_saída ), .A(US), .B(4'b0000));
  and and_1 (ZEROU, \igual_1_saída , \igual_2_saída , \igual_3_saída , \igual_4_saída );
endmodule

// CRONO
module CRONOMETRO (
  input  CLK,
  input  CLK_DM,
  input  CLK_UM,
  input  CLK_DS,
  input  CLK_US,
  input  CLEAR_PRESET,
  input  ENABLE,
  input  ACTIVATE_PRESET,
  input  CLEAR,
  output [3:0] DM,
  output [3:0] UM,
  output [3:0] DS,
  output [3:0] US,
  output ZEROU
);

  wire and_1_out;
  wire [3:0] \preset_1_saída , \preset_2_saída , \preset_3_saída , \preset_4_saída ;

  Hex_Digit_Display hex_digit_display_1 (.value(\preset_1_saída ));  // open: dp
  PRESET preset_1 (.CLK(CLK_DM), .MAXIMO(4'b0110), .CLEAR(CLEAR_PRESET), .\SAÍDA (\preset_1_saída ));
  PRESET preset_2 (.CLK(CLK_UM), .MAXIMO(4'b1010), .CLEAR(CLEAR_PRESET), .\SAÍDA (\preset_2_saída ));
  PRESET preset_3 (.CLK(CLK_DS), .MAXIMO(4'b0110), .CLEAR(CLEAR_PRESET), .\SAÍDA (\preset_3_saída ));
  PRESET preset_4 (.CLK(CLK_US), .MAXIMO(4'b1010), .CLEAR(CLEAR_PRESET), .\SAÍDA (\preset_4_saída ));
  Hex_Digit_Display hex_digit_display_2 (.value(\preset_2_saída ));  // open: dp
  Hex_Digit_Display hex_digit_display_3 (.value(\preset_3_saída ));  // open: dp
  Hex_Digit_Display hex_digit_display_4 (.value(\preset_4_saída ));  // open: dp
  and and_1 (and_1_out, ENABLE, ~ZEROU);  // AND_Gate
  CONTADOR_REGRESSIVO contador_regressivo_1 (
    .CLK(CLK), .PRESET_US(\preset_4_saída ), .PRESET_DS(\preset_3_saída ), .PRESET_UM(\preset_2_saída ),
    .PRESET_DM(\preset_1_saída ), .ENABLE(and_1_out), .ACTIVATE_PRESET(ACTIVATE_PRESET), .CLEAR(CLEAR),
    .US(US), .DS(DS), .UM(UM), .DM(DM), .ZEROU(ZEROU));
endmodule

module CORE (
  input  [3:0] A,
  input  [3:0] B,
  input  PROXIMO,
  input  ZEROU_A,
  input  ZEROU_B,
  input  CHUTAR,
  input  CLOCK_GERADOR,
  output A_JOGANDO,
  output B_JOGANDO,
  output [3:0] \SAÍDA_X ,
  output MAIOR,
  output IGUAL,
  output MENOR,
  output [3:0] \SAÍDA_Y ,
  output [3:0] X_REAL,
  output CHUTANDO_X,
  output CHUTANDO_Y,
  output ACERTOU,
  output [3:0] Y_REAL,
  output [3:0] SOMA
);

  wire and_1_out, and_2_out, circuito_proximo_1_troca_jogador, comparador_2_igual, comparador_3_igual,
       or_1_out, or_2_out;
  wire [3:0] adder_2_out, circuito_proximo_1_out_6;

  not not_1 (A_JOGANDO, B_JOGANDO);
  Hex_Digit_Display hex_digit_display_1 (.value(circuito_proximo_1_out_6));  // open: dp
  CIRCUITO_PROXIMO circuito_proximo_1 (
    .A(A), .B(B), .PROXIMO(PROXIMO), .out_6(circuito_proximo_1_out_6), .JOGADOR_ATUAL(B_JOGANDO),
    .CHUTANDO_Y(CHUTANDO_Y), .CHUTANDO_X(CHUTANDO_X), .TROCA_JOGADOR(circuito_proximo_1_troca_jogador),
    .ZEROU_A(ZEROU_A), .ZEROU_B(ZEROU_B));
  or or_1 (or_1_out, CHUTANDO_Y, CHUTAR);
  or or_2 (or_2_out, CHUTAR, circuito_proximo_1_troca_jogador);
  Register #(.width(4)) register_1 (.D(circuito_proximo_1_out_6), .Q(\SAÍDA_X ), .clk(and_1_out));  // open: en, clr
  and and_1 (and_1_out, or_1_out, CHUTANDO_X);
  Register #(.width(4)) register_2 (.D(circuito_proximo_1_out_6), .Q(\SAÍDA_Y ), .clk(and_2_out));  // open: en, clr
  and and_2 (and_2_out, or_2_out, CHUTANDO_Y);
  Hex_Digit_Display hex_digit_display_2 (.value(X_REAL));  // open: dp
  Random #(.width(4)) random_1 (.clk(CLOCK_GERADOR), .out(X_REAL));  // open: next, clr
  Random #(.width(4)) random_2 (.clk(CLOCK_GERADOR), .out(Y_REAL), .clr(CLOCK_GERADOR));  // open: next
  Hex_Digit_Display hex_digit_display_3 (.value(Y_REAL));  // open: dp
  Adder #(.width(4)) adder_1 (.a(X_REAL), .b(Y_REAL), .out(SOMA));  // open: cin, cout
  Adder #(.width(4)) adder_2 (.a(\SAÍDA_X ), .b(\SAÍDA_Y ), .out(adder_2_out));  // open: cin, cout
  COMPARADOR comparador_1 (.A(adder_2_out), .B(SOMA), .ENABLE(CHUTANDO_X), .MAIOR(MAIOR), .IGUAL(IGUAL), .MENOR(MENOR));
  COMPARADOR comparador_2 (.A(\SAÍDA_X ), .B(X_REAL), .ENABLE(1'b1), .IGUAL(comparador_2_igual));  // open: MAIOR, MENOR
  COMPARADOR comparador_3 (.A(\SAÍDA_Y ), .B(Y_REAL), .ENABLE(1'b1), .IGUAL(comparador_3_igual));  // open: MAIOR, MENOR
  and and_3 (ACERTOU, comparador_2_igual, comparador_3_igual);

  // Notes on the sheet:
  //   REGISTRA X
  //   REGISTRA Y
  //   VALOR REAL X
  //   VALOR REAL Y
endmodule

// PROX
module CIRCUITO_PROXIMO (
  input  [3:0] A,
  input  ZEROU_A,
  input  [3:0] B,
  input  ZEROU_B,
  input  PROXIMO,
  output [3:0] out_6,
  output JOGADOR_ATUAL,
  output TROCA_JOGADOR,
  output CHUTANDO_Y,
  output CHUTANDO_X
);

  wire and_1_out, not_1_out;
  wire [3:0] adder_1_out, \mux_1_saída , \mux_2_saída , \mux_3_saída , register_1_q;

  Register #(.width(4)) register_1 (.D(adder_1_out), .Q(register_1_q), .clk(PROXIMO), .clr(TROCA_JOGADOR));  // open: en
  Adder #(.width(4)) adder_1 (.a(register_1_q), .b(4'b0001), .out(adder_1_out));  // open: cin, cout
  not not_1 (not_1_out, JOGADOR_ATUAL);
  IGUAL igual_1 (.\SAÍDA (TROCA_JOGADOR), .A(adder_1_out), .B(4'b0011));
  IGUAL igual_2 (.\SAÍDA (CHUTANDO_Y), .A(adder_1_out), .B(4'b0010));
  IGUAL igual_3 (.\SAÍDA (CHUTANDO_X), .A(adder_1_out), .B(4'b0001));
  D_Flip_Flop d_ff_1 (.clk(TROCA_JOGADOR), .D(not_1_out), .Q(JOGADOR_ATUAL));  // open: Qn, preset, en, reset
  MUX mux_1 (.A(A), .B(B), .SELETOR(ZEROU_A), .\SAÍDA (\mux_1_saída ));
  MUX mux_2 (.A(B), .B(A), .SELETOR(ZEROU_B), .\SAÍDA (\mux_2_saída ));
  MUX mux_3 (.A(\mux_1_saída ), .B(\mux_2_saída ), .SELETOR(JOGADOR_ATUAL), .\SAÍDA (\mux_3_saída ));
  MUX mux_4 (.A(\mux_3_saída ), .B(4'b0000), .SELETOR(and_1_out), .\SAÍDA (out_6));
  and and_1 (and_1_out, ZEROU_B, ZEROU_A);
  Hex_Digit_Display hex_digit_display_1 (.value(out_6));  // open: dp
endmodule

// >
module MAIOR (
  input  [3:0] A,
  input  [3:0] B,
  output out_3
);

  wire and_1_out, and_2_out, and_3_out, and_4_out, xnor_1_out, xnor_2_out, xnor_3_out;

  and and_1 (and_1_out, A[3], ~B[3]);  // AND_Gate
  xnor xnor_1 (xnor_1_out, A[3], B[3]);
  xnor xnor_2 (xnor_2_out, A[2], B[2]);
  and and_2 (and_2_out, xnor_1_out, A[2], ~B[2]);  // AND_Gate
  and and_3 (and_3_out, xnor_1_out, xnor_2_out, A[1], ~B[1]);  // AND_Gate
  xnor xnor_3 (xnor_3_out, A[1], B[1]);
  and and_4 (and_4_out, xnor_3_out, xnor_1_out, xnor_2_out, A[0], ~B[0]);  // AND_Gate
  or or_1 (out_3, and_1_out, and_2_out, and_3_out, and_4_out);

  // Notes on the sheet:
  //   Compara se A é maior que B
  //   A3=B3
  //   A2=B2
endmodule

// <
module MENOR (
  input  [3:0] A,
  input  [3:0] B,
  output out_3
);

  wire \igual_1_saída , maior_1_out_3;

  MAIOR maior_1 (.A(A), .B(B), .out_3(maior_1_out_3));
  IGUAL igual_1 (.\SAÍDA (\igual_1_saída ), .A(B), .B(A));
  nor nor_1 (out_3, maior_1_out_3, \igual_1_saída );
endmodule

// COMP
module COMPARADOR (
  input  [3:0] A,
  input  [3:0] B,
  input  ENABLE,
  output MAIOR,
  output IGUAL,
  output MENOR
);

  wire and_1_out, and_2_out, and_3_out, and_4_out, and_5_out, and_6_out, and_7_out, and_8_out,
       \igual_1_saída , maior_1_out_3, maior_2_out_3, menor_1_out_3, menor_2_out_3, negativo_1_neg,
       negativo_2_neg, or_1_out, or_2_out, or_3_out;
  wire [3:0] negativo_1_out_2, negativo_2_out_2;

  NEGATIVO negativo_1 (.A(A), .out_2(negativo_1_out_2), .NEG(negativo_1_neg));
  NEGATIVO negativo_2 (.A(B), .out_2(negativo_2_out_2), .NEG(negativo_2_neg));
  LED led_1 (.in(negativo_1_neg));
  Hex_Digit_Display hex_digit_display_1 (.value(negativo_1_out_2));  // open: dp
  LED led_2 (.in(negativo_2_neg));
  Hex_Digit_Display hex_digit_display_2 (.value(negativo_2_out_2));  // open: dp
  and and_1 (and_1_out, negativo_1_neg, ~negativo_2_neg);  // AND_Gate
  IGUAL igual_1 (.\SAÍDA (\igual_1_saída ), .A(negativo_1_out_2), .B(negativo_2_out_2));
  MAIOR maior_1 (.A(negativo_1_out_2), .B(negativo_2_out_2), .out_3(maior_1_out_3));
  MENOR menor_1 (.A(negativo_1_out_2), .B(negativo_2_out_2), .out_3(menor_1_out_3));
  MENOR menor_2 (.A(negativo_1_out_2), .B(negativo_2_out_2), .out_3(menor_2_out_3));
  MAIOR maior_2 (.A(negativo_1_out_2), .B(negativo_2_out_2), .out_3(maior_2_out_3));
  and and_2 (and_2_out, ~negativo_1_neg, negativo_2_neg);  // AND_Gate
  and and_3 (and_3_out, negativo_1_neg, negativo_2_neg, menor_2_out_3);
  and and_4 (and_4_out, ~negativo_1_neg, ~negativo_2_neg, maior_2_out_3);  // AND_Gate
  and and_5 (and_5_out, negativo_1_neg, negativo_2_neg, maior_1_out_3);
  and and_6 (and_6_out, ~negativo_1_neg, ~negativo_2_neg, menor_1_out_3);  // AND_Gate
  and and_7 (and_7_out, \igual_1_saída , negativo_1_neg, negativo_2_neg);
  and and_8 (and_8_out, \igual_1_saída , ~negativo_1_neg, ~negativo_2_neg);  // AND_Gate
  or or_1 (or_1_out, and_2_out, and_3_out, and_4_out);
  or or_2 (or_2_out, and_7_out, and_8_out);
  or or_3 (or_3_out, and_5_out, and_6_out, and_1_out);
  and and_9 (MAIOR, or_1_out, ENABLE);
  and and_10 (IGUAL, or_2_out, ENABLE);
  and and_11 (MENOR, or_3_out, ENABLE);
endmodule

// NEG
module NEGATIVO (
  input  [3:0] A,
  output [3:0] out_2,
  output NEG
);

  wire and_1_out, and_2_out, and_4_out, and_5_out, and_6_out, and_7_out, and_8_out, and_9_out, not_1_out,
       not_2_out, not_3_out, not_4_out, not_5_out, not_6_out, not_7_out, not_8_out, not_9_out;

  not not_1 (not_1_out, A[2]);
  not not_2 (not_2_out, A[1]);
  not not_3 (not_3_out, A[3]);
  not not_4 (not_4_out, A[1]);
  not not_5 (not_5_out, A[0]);
  not not_6 (not_6_out, A[2]);
  not not_7 (not_7_out, A[3]);
  not not_8 (not_8_out, A[0]);
  not not_9 (not_9_out, A[1]);
  and and_1 (and_1_out, A[3], A[1]);
  and and_2 (and_2_out, A[3], A[2]);
  and and_3 (out_2[3], A[3], not_1_out, not_2_out);
  and and_4 (and_4_out, not_3_out, A[2]);
  and and_5 (and_5_out, A[2], not_4_out, not_5_out);
  and and_6 (and_6_out, A[3], not_6_out, A[1]);
  and and_7 (and_7_out, not_7_out, A[1]);
  and and_8 (and_8_out, A[1], not_8_out);
  and and_9 (and_9_out, A[3], A[2], not_9_out, A[0]);
  or or_1 (NEG, and_1_out, and_2_out);
  or or_2 (out_2[2], and_4_out, and_5_out, and_6_out);
  or or_3 (out_2[1], and_7_out, and_8_out, and_9_out);

  assign out_2[0] = A[0];
endmodule

module RELOGIOS (
  input  DMA,
  input  UMA,
  input  DSA,
  input  USA,
  input  DMA_2,
  input  UMA_2,
  input  DSA_2,
  input  USA_2,
  input  START,
  input  CLK,
  input  MODE,
  input  RESET,
  input  SWITCH_PLAYER,
  output [3:0] DMA_3,
  output [3:0] UMA_3,
  output [3:0] DSA_3,
  output [3:0] USA_3,
  output [3:0] DMB,
  output [3:0] UMB,
  output [3:0] DSB,
  output [3:0] USB,
  output ZEROU_A,
  output ZEROU_B
);

  wire and_1_out, d_ff_1_q, d_ff_1_qn, d_ff_2_q, d_ff_2_qn, d_ff_3_q, d_ff_3_qn, multiplexer_1_out,
       multiplexer_2_out, not_1_out, or_1_out, or_2_out, or_3_out, or_4_out;

  D_Flip_Flop d_ff_1 (.clk(START), .D(d_ff_1_qn), .Q(d_ff_1_q), .Qn(d_ff_1_qn));  // open: preset, en, reset
  and and_1 (and_1_out, d_ff_1_q, CLK);
  D_Flip_Flop d_ff_2 (.clk(MODE), .D(d_ff_2_qn), .Q(d_ff_2_q), .Qn(d_ff_2_qn));  // open: preset, en, reset
  D_Flip_Flop d_ff_3 (.clk(SWITCH_PLAYER), .D(d_ff_3_qn), .Q(d_ff_3_q), .Qn(d_ff_3_qn));  // open: preset, en, reset
  or or_1 (or_1_out, DMA, DMA_2);
  or or_2 (or_2_out, UMA, UMA_2);
  or or_3 (or_3_out, DSA, DSA_2);
  or or_4 (or_4_out, USA, USA_2);
  not not_1 (not_1_out, d_ff_3_q);
  Multiplexer #(.enable("false")) multiplexer_1 (.in0(not_1_out), .in1(1'b1), .out(multiplexer_1_out), .sel(ZEROU_B));
  CRONOMETRO cronometro_1 (
    .CLK(and_1_out), .CLK_DM(or_1_out), .CLK_UM(or_2_out), .CLK_DS(or_3_out), .CLK_US(or_4_out), .DM(DMA_3),
    .UM(UMA_3), .DS(DSA_3), .US(USA_3), .CLEAR_PRESET(RESET), .ENABLE(multiplexer_1_out),
    .ACTIVATE_PRESET(d_ff_2_q), .CLEAR(RESET), .ZEROU(ZEROU_A));
  CRONOMETRO cronometro_2 (
    .CLK(and_1_out), .CLK_DM(or_1_out), .CLK_UM(or_2_out), .CLK_DS(or_3_out), .CLK_US(or_4_out), .DM(DMB),
    .UM(UMB), .DS(DSB), .US(USB), .CLEAR_PRESET(RESET), .ENABLE(multiplexer_2_out),
    .ACTIVATE_PRESET(d_ff_2_q), .CLEAR(RESET), .ZEROU(ZEROU_B));
  Multiplexer #(.enable("false")) multiplexer_2 (.in0(d_ff_3_q), .in1(1'b1), .out(multiplexer_2_out), .sel(ZEROU_A));
endmodule

module PLACAR (
  input  CLK,
  input  RESET,
  output [3:0] \SAÍDA 
);

  wire [3:0] adder_1_out;

  Register #(.width(4)) register_1 (.D(adder_1_out), .Q(\SAÍDA ), .clk(CLK), .clr(RESET));  // open: en
  Adder #(.width(4)) adder_1 (.a(\SAÍDA ), .b(4'b0001), .out(adder_1_out));  // open: cin, cout
endmodule
