// Logisim project circuito.circ as structural Verilog: 9 circuits, main circuit main
module main (
  input  in_1,
  input  in_2,
  input  in_3,
  input  in_4,
  input  in_5,
  input  in_6,
  input  in_7,
  input  in_8,
  input  Jogador_Atual,
  input  Jogarl
);

  wire game_1_igual, game_1_maior, game_1_menor;
  wire [2:0] decodificador_1_out_3, decodificador_2_out_3;
  wire [3:0] decodificador_1_out_2, decodificador_2_out_2;

  decodificador decodificador_1 (
    .in_1({in_4, in_3, in_2, in_1}), .out_2(decodificador_1_out_2), .out_3(decodificador_1_out_3));
  decodificador decodificador_2 (
    .in_1({in_8, in_7, in_6, in_5}), .out_2(decodificador_2_out_2), .out_3(decodificador_2_out_3));
  _7_Segment_Display u_7_segment_display_1 (
    .g(decodificador_1_out_2[3]), .f(decodificador_1_out_2[2]), .a(decodificador_1_out_2[1]),
    .b(decodificador_1_out_2[0]), .e(decodificador_1_out_3[0]), .d(decodificador_1_out_3[1]),
    .c(decodificador_1_out_3[2]));  // open: dp
  _7_Segment_Display u_7_segment_display_2 (
    .g(decodificador_2_out_2[3]), .f(decodificador_2_out_2[2]), .a(decodificador_2_out_2[1]),
    .b(decodificador_2_out_2[0]), .e(decodificador_2_out_3[0]), .d(decodificador_2_out_3[1]),
    .c(decodificador_2_out_3[2]));  // open: dp
  game game_1 (
    .A3(in_1), .A2(in_2), .A1(in_3), .A0(in_4), .B3(in_5), .B2(in_6), .B1(in_7), .B0(in_8),
    .Seletor(Jogador_Atual), .Power(Jogarl), .Maior(game_1_maior), .igual(game_1_igual), .Menor(game_1_menor));
  LED led_1 (.in(game_1_maior));
  LED led_2 (.in(game_1_igual));
  LED led_3 (.in(game_1_menor));

  // Notes on the sheet:
  //   Jogador 0
  //   Jogador 1
  //   Palpite do
  //   Jogador 0
  //   Palpite do
  //   Jogador 1
  //   Maior
  //   igual
  //   Menor
endmodule

module multiplexador (
  input  A,
  input  B,
  input  Seletor,
  output \Saída 
);

  wire and_1_out, and_2_out;

  and and_1 (and_1_out, A, ~Seletor);  // AND_Gate
  and and_2 (and_2_out, B, Seletor);
  or or_1 (\Saída , and_1_out, and_2_out);
endmodule

module comparador_igual (
  input  A3,
  input  A2,
  input  A1,
  input  A0,
  input  B3,
  input  B2,
  input  B1,
  input  B0,
  output out_9
);

  wire xnor_1_out, xnor_2_out, xnor_3_out, xnor_4_out;

  xnor xnor_1 (xnor_1_out, A3, B3);
  xnor xnor_2 (xnor_2_out, A2, B2);
  xnor xnor_3 (xnor_3_out, A1, B1);
  xnor xnor_4 (xnor_4_out, A0, B0);
  and and_1 (out_9, xnor_1_out, xnor_2_out, xnor_3_out, xnor_4_out);

  // Notes on the sheet:
  //   Compara se dois números (A e B) são iguais
endmodule

module comparador_maior (
  input  A3,
  input  A2,
  input  A1,
  input  A0,
  input  B3,
  input  B2,
  input  B1,
  input  B0,
  output out_9
);

  wire and_1_out, and_2_out, and_3_out, and_4_out, xnor_1_out, xnor_2_out, xnor_3_out;

  and and_1 (and_1_out, A3, ~B3);  // AND_Gate
  xnor xnor_1 (xnor_1_out, A3, B3);
  xnor xnor_2 (xnor_2_out, A2, B2);
  and and_2 (and_2_out, xnor_1_out, A2, ~B2);  // AND_Gate
  and and_3 (and_3_out, xnor_1_out, xnor_2_out, A1, ~B1);  // AND_Gate
  xnor xnor_3 (xnor_3_out, A1, B1);
  and and_4 (and_4_out, xnor_3_out, xnor_1_out, xnor_2_out, A0, ~B0);  // AND_Gate
  or or_1 (out_9, and_1_out, and_2_out, and_3_out, and_4_out);

  // Notes on the sheet:
  //   A3=B3
  //   A2=B2
  //   Compara se A é maior que B
endmodule

module comparador (
  input  A3,
  input  A2,
  input  A1,
  input  A0,
  input  B3,
  input  B2,
  input  B1,
  input  B0,
  output Maior,
  output igual,
  output Menor
);

  comparador_maior comparador_maior_1 (
    .A3(A3), .A2(A2), .A1(A1), .A0(A0), .B3(B3), .B2(B2), .B1(B1), .B0(B0), .out_9(Maior));
  comparador_igual comparador_igual_1 (
    .A3(A3), .A2(A2), .A1(A1), .A0(A0), .B3(B3), .B2(B2), .B1(B1), .B0(B0), .out_9(igual));
  comparador_menor comparador_menor_1 (
    .A3(A3), .A2(A2), .A1(A1), .A0(A0), .B3(B3), .B2(B2), .B1(B1), .B0(B0), .out_9(Menor));
endmodule

module comparador_menor (
  input  A3,
  input  A2,
  input  A1,
  input  A0,
  input  B3,
  input  B2,
  input  B1,
  input  B0,
  output out_9
);

  wire comparador_igual_1_out_9, comparador_maior_1_out_9;

  comparador_igual comparador_igual_1 (
    .A3(A3), .A2(A2), .A1(A1), .A0(A0), .B3(B3), .B2(B2), .B1(B1), .B0(B0), .out_9(comparador_igual_1_out_9));
  comparador_maior comparador_maior_1 (
    .A3(A3), .A2(A2), .A1(A1), .A0(A0), .B3(B3), .B2(B2), .B1(B1), .B0(B0), .out_9(comparador_maior_1_out_9));
  nor nor_1 (out_9, comparador_igual_1_out_9, comparador_maior_1_out_9);
endmodule

module multiplexador_4_bits (
  input  A3,
  input  A2,
  input  A1,
  input  A0,
  input  B3,
  input  B2,
  input  B1,
  input  B0,
  input  Seletor,
  output out_10,
  output out_11,
  output out_12,
  output out_13
);

  multiplexador multiplexador_1 (.A(A3), .B(B3), .Seletor(Seletor), .\Saída (out_10));
  multiplexador multiplexador_2 (.A(A2), .B(B2), .Seletor(Seletor), .\Saída (out_11));
  multiplexador multiplexador_3 (.A(A1), .B(B1), .Seletor(Seletor), .\Saída (out_12));
  multiplexador multiplexador_4 (.A(A0), .B(B0), .Seletor(Seletor), .\Saída (out_13));
endmodule

module game (
  input  A3,
  input  A2,
  input  A1,
  input  A0,
  input  B3,
  input  B2,
  input  B1,
  input  B0,
  input  Seletor,
  input  Power,
  output Maior,
  output igual,
  output Menor
);

  wire comparador_1_igual, comparador_1_maior, comparador_1_menor, multiplexador_4_bits_1_out_10,
       multiplexador_4_bits_1_out_11, multiplexador_4_bits_1_out_12, multiplexador_4_bits_1_out_13;

  multiplexador_4_bits multiplexador_4_bits_1 (
    .A3(A3), .A2(A2), .A1(A1), .A0(A0), .B3(B3), .B2(B2), .B1(B1), .B0(B0), .Seletor(Seletor),
    .out_10(multiplexador_4_bits_1_out_10), .out_11(multiplexador_4_bits_1_out_11),
    .out_12(multiplexador_4_bits_1_out_12), .out_13(multiplexador_4_bits_1_out_13));
  comparador comparador_1 (
    .A3(multiplexador_4_bits_1_out_10), .A2(multiplexador_4_bits_1_out_11),
    .A1(multiplexador_4_bits_1_out_12), .A0(multiplexador_4_bits_1_out_13), .B3(1'b0), .B2(1'b1), .B1(1'b0),
    .B0(1'b1), .Maior(comparador_1_maior), .igual(comparador_1_igual), .Menor(comparador_1_menor));
  and and_1 (Maior, comparador_1_maior, Power);
  and and_2 (igual, comparador_1_igual, Power);
  and and_3 (Menor, comparador_1_menor, Power);

  // Notes on the sheet:
  //   Número mágico
endmodule

module decodificador (
  input  [3:0] in_1,
  output [3:0] out_2,
  output [2:0] out_3
);

  wire and_1_out, and_2_out, and_3_out, and_4_out, and_5_out, and_6_out, and_7_out, and_8_out, and_9_out,
       and_10_out, and_11_out, and_12_out, and_13_out, and_14_out, and_15_out, and_16_out, and_17_out,
       and_18_out, and_19_out, and_20_out, and_21_out, and_22_out, and_23_out, and_24_out, and_25_out,
       and_26_out, and_27_out, and_28_out, and_29_out, and_30_out, and_31_out, and_32_out, and_33_out,
       and_34_out, and_35_out, and_36_out, and_37_out, and_38_out, and_39_out, and_40_out, or_7_out;

  and and_1 (and_1_out, in_1[2], ~in_1[3]);  // AND_Gate
  and and_2 (and_2_out, in_1[2], ~in_1[0], in_1[3]);  // AND_Gate
  and and_3 (and_3_out, in_1[1], in_1[2], in_1[3]);
  and and_4 (and_4_out, ~in_1[0], in_1[1], in_1[3]);  // AND_Gate
  and and_5 (and_5_out, in_1[0], ~in_1[2], ~in_1[3]);  // AND_Gate
  and and_6 (and_6_out, in_1[0], ~in_1[1], ~in_1[2]);  // AND_Gate
  and and_7 (and_7_out, ~in_1[1], ~in_1[2], ~in_1[3]);  // AND_Gate
  and and_8 (and_8_out, ~in_1[0], ~in_1[1]);  // AND_Gate
  and and_9 (and_9_out, ~in_1[0], ~in_1[2], ~in_1[3]);  // AND_Gate
  and and_10 (and_10_out, ~in_1[0], in_1[2], in_1[3]);  // AND_Gate
  and and_11 (and_11_out, in_1[0], ~in_1[2], in_1[3]);  // AND_Gate
  and and_12 (and_12_out, in_1[0], ~in_1[1], ~in_1[2]);  // AND_Gate
  and and_13 (and_13_out, ~in_1[1], in_1[2], ~in_1[3]);  // AND_Gate
  and and_14 (and_14_out, in_1[0], ~in_1[1]);  // AND_Gate
  and and_15 (and_15_out, in_1[3], ~in_1[2]);  // AND_Gate
  and and_16 (and_16_out, in_1[1], ~in_1[0]);  // AND_Gate
  and and_17 (and_17_out, ~in_1[0], ~in_1[2], ~in_1[3]);  // AND_Gate
  and and_18 (and_18_out, ~in_1[0], in_1[2], in_1[3]);  // AND_Gate
  and and_19 (and_19_out, in_1[0], ~in_1[2], ~in_1[3]);  // AND_Gate
  and and_20 (and_20_out, in_1[1], in_1[2], ~in_1[3]);  // AND_Gate
  and and_21 (and_21_out, in_1[1], ~in_1[2], in_1[3]);  // AND_Gate
  and and_22 (and_22_out, ~in_1[0], ~in_1[1], ~in_1[3]);  // AND_Gate
  and and_23 (and_23_out, ~in_1[1], in_1[3], in_1[0]);  // AND_Gate
  and and_24 (and_24_out, in_1[2], ~in_1[1], ~in_1[0]);  // AND_Gate
  and and_25 (and_25_out, in_1[2], ~in_1[3]);  // AND_Gate
  and and_26 (and_26_out, in_1[0], in_1[1]);
  and and_27 (and_27_out, ~in_1[1], ~in_1[2], ~in_1[3]);  // AND_Gate
  and and_28 (and_28_out, in_1[0], in_1[2], in_1[3]);
  and and_29 (and_29_out, ~in_1[2], ~in_1[3]);  // AND_Gate
  and and_30 (and_30_out, in_1[0], ~in_1[1]);  // AND_Gate
  and and_31 (and_31_out, in_1[0], in_1[1], in_1[2]);
  and and_32 (and_32_out, ~in_1[0], in_1[1], ~in_1[2]);  // AND_Gate
  and and_33 (and_33_out, in_1[1], in_1[2], ~in_1[3]);  // AND_Gate
  and and_34 (and_34_out, in_1[0], ~in_1[1]);  // AND_Gate
  and and_35 (and_35_out, in_1[2], ~in_1[3]);  // AND_Gate
  and and_36 (and_36_out, in_1[0], in_1[1], in_1[3]);
  and and_37 (and_37_out, in_1[0], in_1[1], ~in_1[2]);  // AND_Gate
  and and_38 (and_38_out, ~in_1[0], ~in_1[1], in_1[2]);  // AND_Gate
  or or_1 (out_2[1], and_1_out, and_2_out, and_3_out, and_4_out, and_5_out, and_6_out, and_7_out);
  or or_2 (out_2[0], and_8_out, and_9_out, and_10_out, and_11_out, and_12_out, and_13_out);
  or or_3 (out_3[2], and_14_out, and_15_out, and_16_out, and_17_out, and_18_out);
  or or_4 (out_3[1], and_19_out, and_20_out, and_21_out, and_22_out, and_23_out, and_24_out);
  or or_5 (out_3[0], and_25_out, and_26_out, and_27_out, and_28_out);
  or or_6 (out_2[2], and_29_out, and_30_out, and_31_out, and_32_out, and_33_out);
  or or_7 (or_7_out, and_34_out, and_35_out, and_36_out, and_37_out, and_38_out);
  and and_39 (and_39_out, ~in_1[0], in_1[1], ~in_1[2], ~in_1[3]);  // AND_Gate
  and and_40 (and_40_out, ~in_1[0], in_1[1], ~in_1[2], in_1[3]);  // AND_Gate
  or or_8 (out_2[3], or_7_out, and_39_out, and_40_out);

  // Notes on the sheet:
  //   *************************************************************************************************************
  //   *************************************************************************************************************
  //   *************************************************************************************************************
  //   *************************************************************************************************************
  //   *************************************************************************************************************
  //   *************************************************************************************************************
  //   circuito do a
  //   circuito do b
  //   circuito do c
  //   circuito do d
  //   circuito do e
  //   circuito do f
  //   circuito do g
endmodule
